# Fritzing sketch PatientAware Schematic (saved by Fritzing 0.9.9b)
circuit board: 8.46667cm x 5.64444cm

parts:
  Mod1 = Raspberry Pi 4B
  INA1 = INA219 DC Current Sensor Breakout
  INA2 = INA219 DC Current Sensor Breakout
  INA3 = INA219 DC Current Sensor Breakout
  INA4 = INA219 DC Current Sensor Breakout
  J1 = female pin header, 2 pins [form="♀ (female)"]
  J2 = female pin header, 2 pins [form="♀ (female)"]
  J3 = female pin header, 2 pins [form="♀ (female)"]
  J4 = female pin header, 2 pins [form="♀ (female)"]

nets:
  VCC: Mod1.3V3, INA1.VCC, INA1.Vin+, INA2.VCC, INA2.Vin+, INA3.VCC, INA3.Vin+, INA4.VCC, INA4.Vin+
  N1: Mod1.GPIO2, INA1.SDA, INA2.SDA, INA3.SDA, INA4.SDA
  N2: Mod1.GPIO3, INA1.SCL, INA2.SCL, INA3.SCL, INA4.SCL
  GND: Mod1.GND, INA1.GND, INA2.GND, INA3.GND, INA4.GND, J1.pin1, J2.pin1, J3.pin1, J4.pin1
  N3: INA1.Vin-, J4.pin2
  N4: INA2.Vin-, J3.pin2
  N5: INA3.Vin-, J2.pin2
  N6: INA4.Vin-, J1.pin2

notes:
  NanoWire Connections
  - +

custom parts:
  INA219 DC Current Sensor Breakout: INA DC Current Sensor Breakout
